// Logisim project L1_PedroRicieriMarchi.circ as structural Verilog: 12 circuits, main circuit 1_1
module _1_1 (
  input  A,
  input  B,
  input  C,
  input  D,
  output S
);

  wire and_1_out, nor_1_out, not_1_out, or_1_out, xnor_1_out, xor_1_out, xor_2_out;

  ExactlyOne xor_1 (.out(xor_1_out), .in0(A), .in1(B), .in2(C), .in3(D));
  and and_1 (and_1_out, ~A, B, C, ~D);  // AND_Gate
  ExactlyOne xor_2 (.out(xor_2_out), .in0(A), .in1(B), .in2(C), .in3(D));
  or or_1 (or_1_out, A, ~B, C, D);  // OR_Gate
  NotExactlyOne xnor_1 (.out(xnor_1_out), .in0(xor_1_out), .in1(and_1_out), .in2(xor_2_out));
  not not_1 (not_1_out, and_1_out);
  nor nor_1 (nor_1_out, xor_2_out, ~or_1_out);  // NOR_Gate
  and and_2 (S, xnor_1_out, not_1_out, nor_1_out);

  // Notes on the sheet:
  //   S = AB + ACD' + AC'D + BC'D + A'B'C'D' + A'B'CD
endmodule

module _1_2 (
  input  A,
  input  B,
  input  C,
  output S
);

  wire and_1_out, and_2_out, not_1_out, or_1_out;

  and and_1 (and_1_out, A, ~C);  // AND_Gate
  or or_1 (or_1_out, A, B, C);
  not not_1 (not_1_out, or_1_out);
  and and_2 (and_2_out, A, ~B, C);  // AND_Gate
  ExactlyOne xor_1 (.out(S), .in0(and_1_out), .in1(not_1_out), .in2(and_2_out));

  // Notes on the sheet:
  //   S = B'C' + AC'+ AB'
endmodule

module _2_1 (
  input  A,
  input  B,
  input  C,
  output out_4
);

  wire and_1_out, or_1_out, or_2_out;

  or or_1 (or_1_out, ~C, B);  // OR_Gate
  or or_2 (or_2_out, C, ~B);  // OR_Gate
  and and_1 (and_1_out, or_1_out, or_2_out);
  or or_3 (out_4, and_1_out, ~A);  // OR_Gate
endmodule

module _2_2 (
  input  A,
  input  B,
  input  C,
  output R
);

  wire and_1_out, and_2_out, and_3_out;

  and and_1 (and_1_out, ~A, B);  // AND_Gate
  and and_2 (and_2_out, B, C);
  and and_3 (and_3_out, C, ~B, A);  // AND_Gate
  or or_1 (R, and_1_out, and_2_out, and_3_out);
endmodule

module _3 (
  input  A0,
  input  B0,
  input  A1,
  input  B1,
  input  A2,
  input  B2,
  input  A3,
  input  B3,
  input  A4,
  input  B4,
  input  A5,
  input  B5,
  input  A6,
  input  B6,
  input  A7,
  input  B7,
  output S0,
  output S1,
  output S2,
  output S3,
  output S4,
  output S5,
  output S6,
  output S7,
  output COUT
);

  wire and_1_out, n3_adder_1_cout, n3_adder_2_cout, n3_adder_3_cout, n3_adder_4_cout, n3_adder_5_cout,
       n3_adder_6_cout;

  and and_1 (and_1_out, B0, A0);
  xor xor_1 (S0, B0, A0);
  _3_adder u_3_adder_1 (.A(A1), .B(B1), .CIN(and_1_out), .SUM(S1), .COUT(n3_adder_1_cout));
  _3_adder u_3_adder_2 (.A(A2), .B(B2), .CIN(n3_adder_1_cout), .SUM(S2), .COUT(n3_adder_2_cout));
  _3_adder u_3_adder_3 (.A(A3), .B(B3), .CIN(n3_adder_2_cout), .SUM(S3), .COUT(n3_adder_3_cout));
  _3_adder u_3_adder_4 (.A(A4), .B(B4), .CIN(n3_adder_3_cout), .SUM(S4), .COUT(n3_adder_4_cout));
  _3_adder u_3_adder_5 (.A(A5), .B(B5), .CIN(n3_adder_4_cout), .SUM(S5), .COUT(n3_adder_5_cout));
  _3_adder u_3_adder_6 (.A(A6), .B(B6), .CIN(n3_adder_5_cout), .SUM(S6), .COUT(n3_adder_6_cout));
  _3_adder u_3_adder_7 (.A(A7), .B(B7), .CIN(n3_adder_6_cout), .SUM(S7), .COUT(COUT));
endmodule

module _3_adder (
  input  A,
  input  B,
  input  CIN,
  output SUM,
  output COUT
);

  wire and_1_out, and_2_out, and_3_out, xor_1_out;

  xor xor_1 (xor_1_out, A, B);
  and and_1 (and_1_out, A, B);
  and and_2 (and_2_out, B, CIN);
  and and_3 (and_3_out, A, CIN);
  xor xor_2 (SUM, xor_1_out, CIN);
  xor xor_3 (COUT, and_1_out, and_2_out, and_3_out);
endmodule

module _4 (
  input  T,
  input  P,
  input  R,
  output LA
);

  wire and_1_out, and_2_out;

  and and_1 (and_1_out, R, T);
  and and_2 (and_2_out, P, T);
  or or_1 (LA, and_1_out, and_2_out);
endmodule

module _5_1 (
  input  A,
  input  B,
  input  C,
  output S
);

  wire and_1_out, and_2_out;

  and and_1 (and_1_out, C, B);
  and and_2 (and_2_out, C, B, A);
  or or_1 (S, and_1_out, and_2_out, A);

  // Notes on the sheet:
  //   S = (CB) + A
endmodule

module _5_2 (
  input  A,
  input  B,
  input  C,
  input  D,
  output S
);

  wire and_1_out, and_2_out, and_3_out, and_4_out;

  and and_1 (and_1_out, B, A);
  and and_2 (and_2_out, C, B, A);
  and and_3 (and_3_out, D, C, B);
  and and_4 (and_4_out, D, C);
  or or_1 (S, and_1_out, and_2_out, and_3_out, and_4_out);

  // Notes on the sheet:
  //   S = (AB) + (CD)
endmodule

module _5_3 (
  input  A,
  input  B,
  input  C,
  output S
);

  wire and_1_out, and_2_out, and_3_out, and_4_out, or_1_out;

  and and_1 (and_1_out, C, A);
  and and_2 (and_2_out, C, B);
  and and_3 (and_3_out, C, B, A);
  and and_4 (and_4_out, C, A);
  or or_1 (or_1_out, and_3_out, and_4_out, and_4_out);
  or or_2 (S, and_1_out, and_2_out, or_1_out);

  // Notes on the sheet:
  //   S = C(A + B)
endmodule

module _6_1 (
  input  A,
  input  B,
  input  C,
  input  D,
  output R,
  output S
);

  wire and_1_out, and_2_out, and_3_out, and_4_out, and_5_out, and_6_out, not_1_out, not_2_out, not_3_out,
       not_4_out, not_5_out, not_6_out, not_7_out;

  not not_1 (not_1_out, A);
  not not_2 (not_2_out, C);
  not not_3 (not_3_out, D);
  not not_4 (not_4_out, B);
  not not_5 (not_5_out, A);
  not not_6 (not_6_out, B);
  not not_7 (not_7_out, C);
  and and_1 (and_1_out, not_1_out, B);
  and and_2 (and_2_out, B, not_2_out, not_3_out);
  and and_3 (and_3_out, A, not_4_out, C);
  and and_4 (and_4_out, not_5_out, not_6_out, C);
  and and_5 (and_5_out, B, not_7_out, D);
  and and_6 (and_6_out, B, A);
  or or_1 (R, and_1_out, and_2_out, and_3_out);
  or or_2 (S, and_4_out, and_5_out, and_6_out);
endmodule

module _6_2 (
  input  A,
  input  B,
  input  C,
  output S
);

  wire and_1_out, xor_1_out;

  xor xor_1 (xor_1_out, A, B);
  and and_1 (and_1_out, C, B);
  or or_1 (S, xor_1_out, and_1_out);
endmodule
