// Logisim project codificadores_Bruno_Camila_Pedro.circ as structural Verilog: 1 circuit, main circuit main
module main (
  input  A,
  input  B,
  input  C,
  input  D,
  output S1,
  output S2,
  output V
);

  wire and_1_out;

  and and_1 (and_1_out, ~B, C);  // AND_Gate
  or or_1 (S1, B, A);
  or or_2 (S2, A, and_1_out);
  or or_3 (V, D, C, B, A);
endmodule
